# Fritzing sketch remote_schematic (saved by Fritzing 0.9.3b)

parts:
  Bauteil1 = Arduino Mega ADK (Rev3)
  Bauteil2 = Bluetooth HC-05 Macho
  Joystick = Thumb Joystick
  R1 = Resistor [tolerance=±5% resistance=1k package="2010 [SMD]"]
  R2 = Resistor [tolerance=±5% resistance=2k package="2010 [SMD]"]

nets:
  N1: Bauteil1.A0, Joystick.VERT
  N2: Bauteil1.A1, Joystick.HORZ
  N3: Bauteil1.D19/RX1, Bauteil2.TXD
  N4: Bauteil1.D18/TX1, R1.Pin_0
  5V: Bauteil1.5V, Joystick.VCC
  GND: Bauteil1.GND, Joystick.GND
  N5: Bauteil2.RXD, R1.Pin_1, R2.Pin_1
